# Fritzing sketch Breadboard layout (saved by Fritzing 0.9.3b)
breadboards: 6

parts:
  DI1 = 7-Segment LED Display [package=THT]
  DI2 = 7-Segment LED Display [package=THT]
  Part1 = Arduino Nano (Rev3.0) (ICSP)  # not connected
  IC1 = IC, DIP package, 14 pins [chip_label=74LS48]
  IC2 = IC, DIP package, 14 pins [chip_label=74LS48]
  IC3 = IC, DIP package, 14 pins [chip_label=74LS164]
  IC4 = IC, DIP package, 14 pins [chip_label=74LS164]
  SW1 = DIP Switch 8 Position [package=dipswitch-08]
  SW2 = DIP Switch 8 Position [package=dipswitch-08]
  SW3 = DIP Switch 8 Position [package=dipswitch-08]
  IC5 = IC, DIP package, 14 pins [chip_label=74LS165]
  IC6 = IC, DIP package, 14 pins [chip_label=74LS165]

nets:
  N1: DI1.commAnode#2, DI2.commAnode#2, IC1.pin7, IC2.pin7
  N2: DI1.commAnode#7, DI2.commAnode#7, IC1.pin14, IC2.pin14
  N3: IC3.pin7, IC4.pin7
  N4: IC3.pin14, IC4.pin14
  N5: SW1.9, SW1.10, SW1.11, SW1.12, SW1.13, SW1.14, SW1.15, SW1.16, SW2.9, SW2.10, SW2.11, SW2.12, SW2.13, SW2.14, SW2.15, SW2.16, SW3.9, SW3.10, SW3.11, SW3.12, SW3.13, SW3.14, SW3.15, SW3.16
  N6: IC5.pin7, IC6.pin7
  N7: IC5.pin14, IC6.pin14
